# Fritzing sketch Devre_semasi (saved by Fritzing 1.0.2b)

parts:
  Parça1 = Arduino Uno (Rev3) - ICSP
  L298N1 = L298N DC motor driver
  M1 = DC Motor [voltage_(max)=6V voltage_(min)=3V]
  M2 = DC Motor [voltage_(max)=6V voltage_(min)=3V]
  M3 = DC Motor [voltage_(max)=6V voltage_(min)=3V]
  M4 = DC Motor [voltage_(max)=6V voltage_(min)=3V]
  VCC1 = Battery block 9V
  Mod1 = KY-022 Infrared Receiver Module [package="Breakout board"]

nets:
  N1: Parça1.D8, L298N1.IN4
  N2: Parça1.D9_PWM, L298N1.IN3
  N3: Parça1.D10_PWM/SS, L298N1.IN2
  N4: Parça1.D11_PWM/MOSI, L298N1.ENA
  N5: Parça1.D12/MISO, L298N1.IN1
  GND: Parça1.GND, L298N1.GND, VCC1.-, Mod1.-
  N6: Parça1.D2, Mod1.S
  N7: Parça1.D6_PWM, L298N1.ENB
  5V: Parça1.5V, Mod1.Vin
  N8: Parça1.VIN, VCC1.+
  N9: L298N1.OUT1, M3.pin_2, M4.pin_2
  N10: L298N1.OUT2, M3.pin_1, M4.pin_1
  N11: L298N1.OUT3, M1.pin_2, M2.pin_2
  N12: L298N1.OUT4, M1.pin_1, M2.pin_1

notes:
  Sol motorlar
  Sağ motorlar
  12V
  Batarya

custom parts:
  L298N DC motor driver: 2x DC motor driver with 78M05 positive voltage regulator (7..35 V) L298N: max 46 V, 2 A Set 5 V Enable jumper to enable 5 V regultor (needed for the L298N) and +5 V output at screw terminal or supply external +5 V at screw terminal Set ENA and/or ENB to +5 V to enable motor permanently or supply ENA and/or ENB with PWM signal IN1 and IN2 set rotation directory for motor A (OUT1/OUT2) IN2 and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
  KY-022 Infrared Receiver Module: KY-022 IR receiver module, reacts to 38kHz infrared light.
